// Logisim project prac_5_lphtum003_jhrsha002.circ as structural Verilog: 2 circuits, main circuit 2b ALU
module _2b_ALU_black_box (
  input  in_1,
  input  in_2,
  input  in_3,
  input  in_4,
  input  NB__set_to_1000,
  input  in_6,
  input  in_7,
  input  in_8,
  input  in_9,
  input  in_10,
  input  in_11,
  input  in_12,
  input  in_13,
  input  in_14,
  input  in_15,
  output out_16,
  output out_17
);

  _2b_ALU u_2b_alu_1 (
    ._1(in_4), ._0(NB__set_to_1000), ._0_2(in_6), ._0_3(in_7), .out_16(out_16), ._1_2(in_12), ._1_3(in_13),
    .out_17(out_17), ._1_4(in_14), ._1_5(in_15), .A1(in_11), .A0(in_10), .B1(in_9), .B0(in_8), .F2(in_1),
    .F1(in_2), .F0(in_3));

  // Notes on the sheet:
  //   NB! set to 1111
endmodule

module _2b_ALU (
  input  A1,
  input  A0,
  input  B1,
  input  B0,
  input  F2,
  input  F1,
  input  F0,
  input  _1,
  input  _0,
  input  _1_2,
  input  _0_2,
  input  _1_3,
  input  _0_3,
  input  _1_4,
  input  _1_5,
  output out_16,
  output out_17
);

  wire adder_1_cout, adder_1_out, adder_2_out, adder_3_cout, adder_3_out, adder_4_out, and_1_out, and_2_out,
       multiplexer_1_out, multiplexer_2_out, multiplexer_3_out, multiplexer_4_out, multiplexer_5_out,
       multiplexer_6_out, multiplexer_7_out, multiplexer_8_out, multiplexer_9_out, multiplexer_10_out,
       multiplexer_11_out, multiplexer_12_out, or_1_out, or_2_out, xor_1_out, xor_2_out, xor_3_out, xor_4_out;

  xor xor_1 (xor_1_out, B0, F0);
  xor xor_2 (xor_2_out, B1, F0);
  xor xor_3 (xor_3_out, _1, F1);
  xor xor_4 (xor_4_out, _0, F0);
  Multiplexer multiplexer_1 (.in0(A1), .in1(A0), .out(multiplexer_1_out), .sel(_1_2), .en(_1_2));
  Multiplexer multiplexer_2 (.in0(A0), .in1(_0_2), .out(multiplexer_2_out), .sel(_1_3), .en(_1_3));
  Multiplexer multiplexer_3 (.in0(A1), .in1(_0_3), .out(multiplexer_3_out), .sel(_1_4), .en(_1_4));
  Multiplexer multiplexer_4 (.in0(A0), .in1(A1), .out(multiplexer_4_out), .sel(_1_5), .en(_1_5));
  and and_1 (and_1_out, B0, A0);
  Multiplexer multiplexer_5 (.in0(and_1_out), .in1(or_1_out), .out(multiplexer_5_out), .sel(F0));  // open: en
  or or_1 (or_1_out, B0, A0);
  and and_2 (and_2_out, B1, A1);
  Multiplexer multiplexer_6 (.in0(and_2_out), .in1(or_2_out), .out(multiplexer_6_out), .sel(F0));  // open: en
  or or_2 (or_2_out, B1, A1);
  Adder #(.width(1)) adder_1 (.a(xor_1_out), .b(A0), .out(adder_1_out), .cin(F0), .cout(adder_1_cout));
  Adder #(.width(1)) adder_2 (.a(xor_2_out), .b(A1), .out(adder_2_out), .cin(adder_1_cout));  // open: cout
  Adder #(.width(1)) adder_3 (.a(xor_3_out), .b(A0), .out(adder_3_out), .cin(F1), .cout(adder_3_cout));
  Adder #(.width(1)) adder_4 (.a(xor_4_out), .b(A1), .out(adder_4_out), .cin(adder_3_cout));  // open: cout
  Multiplexer multiplexer_7 (
    .in0(multiplexer_2_out), .in1(multiplexer_4_out), .out(multiplexer_7_out), .sel(F0));  // open: en
  Multiplexer multiplexer_8 (
    .in0(multiplexer_1_out), .in1(multiplexer_3_out), .out(multiplexer_8_out), .sel(F0));  // open: en
  Multiplexer multiplexer_9 (.in0(adder_1_out), .in1(adder_3_out), .out(multiplexer_9_out), .sel(F1));  // open: en
  Multiplexer multiplexer_10 (.in0(adder_2_out), .in1(adder_4_out), .out(multiplexer_10_out), .sel(F1));  // open: en
  Multiplexer multiplexer_11 (
    .in0(multiplexer_7_out), .in1(multiplexer_5_out), .out(multiplexer_11_out), .sel(F1));  // open: en
  Multiplexer multiplexer_12 (
    .in0(multiplexer_8_out), .in1(multiplexer_6_out), .out(multiplexer_12_out), .sel(F1));  // open: en
  Multiplexer multiplexer_13 (.in0(multiplexer_9_out), .in1(multiplexer_11_out), .out(out_16), .sel(F2));  // open: en
  Multiplexer multiplexer_14 (.in0(multiplexer_10_out), .in1(multiplexer_12_out), .out(out_17), .sel(F2));  // open: en
endmodule
